# Fritzing sketch night_light (saved by Fritzing 0.9.3b)
breadboards: 1

parts:
  Part1 = Arduino Uno (Rev3)
  LED2 = LED - 5mm [color="White (4500K)" package="5 mm [THT]"]
  LED3 = LED - 5mm [color="White (4500K)" package="5 mm [THT]"]
  LED1 = smd LED [color="Orange (620nm)" package="0603 [SMD]"]
  LED1_2 = smd LED [color="White (4500K)" package="0805 [SMD]"]
  R1 = Photocell (LDR) [package=THT]
  U1 = POT [package=alps_pot]
  R2 = Resistor [tolerance=±5% resistance=220 package=THT]
  R3 = Resistor [tolerance=±5% resistance=220 package=THT]
  R4 = Resistor [tolerance=±5% resistance=220 package=THT]
  R5 = Resistor [tolerance=±5% resistance=10k package=THT]

nets:
  N1: Part1.A0, R1.pin_0, R5.Pin_1
  N2: Part1.A1, U1.S
  N3: Part1.D8, LED2.anode
  N4: Part1.D9_PWM, LED1.anode, LED1_2.anode
  N5: Part1.D7, LED3.anode
  N6: Part1.5V, R1.pin_1, U1.A
  N7: Part1.GND, U1.E, R2.Pin_0, R3.Pin_0, R4.Pin_0, R5.Pin_0
  N8: LED2.cathode, R3.Pin_1
  N9: LED3.cathode, R4.Pin_1
  N10: LED1.cathode, LED1_2.cathode, R2.Pin_1
